# Fritzing sketch hifi-remote (saved by Fritzing 0.9.2b)

parts:
  Part1 = Arduino Pro Mini v13
  D1 = LTE-302 [package=lte-302]
  IR1 = TSOP312.., 314.. [package=THT]
  U3 = mystery part, 3 pins [chip_label=?]
  R1 = Resistor [tolerance=±5% resistance=220 package="0402 [SMD]"]

nets:
  N1: Part1.VCC, IR1.Vs, U3.pin3
  GND: Part1.GND, D1.C, IR1.GND, U3.pin2
  N2: Part1.D11_PWM/MOSI, IR1.Data
  N3: Part1.D3_PWM, R1.Pin_1
  N4: Part1.D2, U3.pin1
  N5: D1.A, R1.Pin_0

notes:
  433mhz receiver
